# Fritzing sketch Devre (saved by Fritzing 0.9.3b)
breadboards: 1

parts:
  LCD1 = LCD screen
  Parça1 = Arduino Uno (Rev3)
  S2 = PH meter [package=THT]
  U1 = Module 4 Relais 5V [package="Module 4 Relais 5V"]
  M1 = DC Motor
  M2 = DC Motor
  M3 = DC Motor
  VCC1 = Battery block 9V
  S3 = PH meter [package=THT]
  S4 = Pushbutton [package="[THT]"]
  LCM1602_IIC1 = LCM1602 IIC [part_number="LCM1602 IIC" chip_label="LCM1602 IIC" package="DIP (Dual Inline) [THT]"]
  S5 = Pushbutton [package="[THT]"]
  S6 = Pushbutton [package="[THT]"]
  R1 = Resistor [tolerance=±5% resistance=220 package=THT]
  R2 = Resistor [tolerance=±5% resistance=220 package=THT]
  R3 = Resistor [tolerance=±5% resistance=220 package=THT]

nets:
  VSS: LCD1.VSS, LCM1602_IIC1.VSS
  VDD: LCD1.VDD, LCM1602_IIC1.VDD
  N1: LCD1.V0, LCM1602_IIC1.V0
  N2: LCD1.RS, LCM1602_IIC1.RS
  N3: LCD1.R/W, LCM1602_IIC1.RW
  N4: LCD1.E, LCM1602_IIC1.E
  N5: LCD1.DB0, LCM1602_IIC1.D0
  N6: LCD1.DB1, LCM1602_IIC1.D1
  N7: LCD1.DB2, LCM1602_IIC1.D2
  N8: LCD1.DB3, LCM1602_IIC1.D3
  N9: LCD1.DB4, LCM1602_IIC1.D4
  N10: LCD1.DB5, LCM1602_IIC1.D5
  N11: LCD1.DB6, LCM1602_IIC1.D6
  N12: LCD1.DB7, LCM1602_IIC1.D7
  N13: LCD1.LED+, LCM1602_IIC1.A
  N14: LCD1.LED-, LCM1602_IIC1.K
  N15: Parça1.A0, S2.pin1
  N16: Parça1.A1, S3.pin1
  N17: Parça1.A4/SDA, LCM1602_IIC1.SDA
  N18: Parça1.A5/SCL, LCM1602_IIC1.SCL
  N19: Parça1.D1/TX, U1.IN1
  N20: Parça1.D2, U1.IN2
  N21: Parça1.D3_PWM, U1.IN3
  N22: Parça1.D4, S4.Pin_1, S4.Pin_2, R1.Pin_0
  N23: Parça1.D5_PWM, S5.Pin_1, S5.Pin_2, R2.Pin_0
  N24: Parça1.D6_PWM, S6.Pin_1, S6.Pin_2, R3.Pin_0
  5V: Parça1.5V, S3.pin2, LCM1602_IIC1.VCC
  N25: S2.pin2, U1.VCC
  N26: S2.pin3, U1.GND, M1.pin_2, VCC1.-, S4.Pin_3, S4.Pin_4, S5.Pin_3, S5.Pin_4, S6.Pin_3, S6.Pin_4, R1.Pin_1, R2.Pin_1, R3.Pin_1
  N27: U1.K1-NF, M1.pin_1
  N28: U1.K2-Com, M2.pin_1
  N29: U1.K3-Com, M3.pin_1
  N30: U1.K3-NO, VCC1.+
  N31: S3.pin3, LCM1602_IIC1.GND

notes:
  ec metre
  ph metre

custom parts:
  Module 4 Relais 5V: Module 4 Relais 5V 4x SPD-06VDC-SD-C
  LCM1602 IIC: I2C-Module to use a 1602 or 2004 LCD on with the wire.h libory Serial LCD Modul

// code stored in the sketch: Untitled2.ino
#include <Wire.h>
#include "DFRobot_EC.h"
DFRobot_EC ec;
#include <LiquidCrystal_I2C.h>
LiquidCrystal_I2C lcd(0x27, 16, 2);

//ekran
int upButton = 7, downButton = 4, selectButton = 5, menu = 1;

//ph sensörü
float calibration_value = 21.34 - 0.7;
int phval = 0; 
unsigned long int avgval; 
int buffer_arr[10],temp;
float ph_act;
float ph ;

//ec sensörü
float voltage,ecValue,temperature = 25;
float AD,EC;
float Ec;

//motor
const int in2 = 2;
const int in3 = 3;
const int in4 = 4;
int bkl = 0;

void setup() {
    //ekran
    lcd.backlight();
    pinMode(upButton, INPUT_PULLUP);
    pinMode(downButton, INPUT_PULLUP);
    pinMode(selectButton, INPUT_PULLUP);
    updateMenu();
  
  //ph sensör
  
  Wire.begin();
  Serial.begin(9600);
  
  //ec sensör
  
  Serial.begin(9600);
  ec.begin();
  
  //motor
  
  pinMode(in2, OUTPUT);
  pinMode(in3, OUTPUT);
  pinMode(in4, OUTPUT);
  
 
}

void loop() 
{


  
//ph sensörü

 for(int i=0;i<10;i++) 
 { 
   buffer_arr[i]=analogRead(A0);
   delay(30);
 }
 for(int i=0;i<9;i++)
 {
   for(int j=i+1;j<10;j++)
   {
     if(buffer_arr[i]>buffer_arr[j])
     {
       temp=buffer_arr[i];
       buffer_arr[i]=buffer_arr[j];
       buffer_arr[j]=temp;
     }
   }
 }
 avgval=0;
 for(int i=2;i<8;i++)
 avgval+=buffer_arr[i];
 float volt=(float)avgval*5.0/1024/6; 
  ph_act = -5.70 * volt + calibration_value;
 
 Serial.print("pH Val: ");
 Serial.println(ph_act);
 delay(1000);
 
//ec semsörü

 char i;
 AD = 0;
 for(i=0;i<20;i++)
 {
    AD = AD + analogRead(0);
    delay(20);
 }
 AD = AD / 20;
 voltage = (AD/1024.0)*5000;
 ecValue = ec.readEC(voltage,temperature); 
 if(ecValue > 0){EC = ecValue;}
 ec.calibration(voltage,temperature); 
 delay(1000);
 Serial.print("EC degeri: ");
 Serial.println(ecValue);
 Serial.print("S?cakl?k: ");
 Serial.println(temperature);



   //sayaç
   for(int sure=0 ; sure = 6 ; sure++){
       delay(300000);//5dk bekle
   }
   
   //motor
   if (ph_act > ph){
   
    digitalWrite(in2,LOW);//çal??t?r motor 1
    delay(bkl);// bekle
    digitalWrite(in2, HIGH );//kapat
    !digitalRead(ph_act);
   }
   
    delay(1000);//1 sn bekle
    
    if(ecValue > Ec){
    digitalWrite(in3, LOW);//çal??t?r motor 2
    delay(bkl);//10sn bekle
    digitalWrite(in3,HIGH );//kapat
    !digitalRead(ecValue);
    }
   
    delay(1000 );//1 sn bekle
    
    if(ecValue <Ec){
    digitalWrite(in4,LOW );//çal??t?r motor 3
    delay(bkl);//10sn bekle
    digitalWrite(in4,HIGH );//kapat
    !digitalRead(ecValue);
    }
   
  if (!digitalRead(downButton))
  {
    menu++;
    updateMenu();
    delay(100);
    while (!digitalRead(downButton));
  }
  if (!digitalRead(upButton))
  {
    menu--;
    updateMenu();
    delay(100);
    while(!digitalRead(upButton));
  }
  if (!digitalRead(selectButton))
  {
    executeAction();
    updateMenu();
    delay(100);
    while (!digitalRead(selectButton));
  }
}

void updateMenu() 
{
  switch (menu)
  {
    case 0:
      menu = 1;
      break;
    case 1:
      lcd.clear();
      lcd.print(">ph sensoru");
      lcd.setCursor(0, 1);
      lcd.print(" ec sensoru");
      break;
    case 2:
      lcd.clear();
      lcd.print(" ph sensoru");
      lcd.setCursor(0, 1);
      lcd.print(">ec sensoru");
      break;
   case 3: 
      lcd.clear();
      lcd.print(">motor hizi");
      lcd.setCursor(0, 1);
      lcd.print(" sicaklik");
      break;
    case 4:
      lcd.clear();
      lcd.print(" motor hizi");
      lcd.setCursor(0, 1);
      lcd.print(">sicaklik");
      break;
    case 5:
      menu = 4;
      break;
  }
}

void executeAction() 
{
  switch (menu) 
  {
    case 1:
      action1();
      break;
    case 2:
      action2();
      break;
      case 3:
      action3();
      break;
    case 4:
      action4();
      break;
    
  }
}

void action1() 
{
  lcd.clear();
  lcd.print(">ph ");
   lcd.setCursor(5, 0);
   lcd.print(ph);
   lcd.setCursor(11, 0);
   lcd.print(ph_act);
  delay(15000);
  //ph buton kodu
  if (!digitalRead(downButton))
  {
   ph++;
    delay(100);
    while (!digitalRead(downButton));
  }
  if (!digitalRead(upButton))
  {
   ph--;
    delay(100);
    while(!digitalRead(upButton));
  }
  if (!digitalRead(selectButton))
  {
    executeAction();
    updateMenu();
    delay(100);
    while (!digitalRead(selectButton));
  }
}
void action2() 
{
   lcd.clear();
   lcd.print(">ec ");
   lcd.setCursor(5, 0);
   lcd.print(Ec);
   lcd.setCursor(11, 0);
   lcd.print(ecValue);
  delay(15000);
  //ec artt?r azalt
  if (!digitalRead(downButton))
  {
    Ec++;
    delay(100);
    while (!digitalRead(downButton));
  }
  if (!digitalRead(upButton))
  {
    Ec--;
    delay(100);
    while(!digitalRead(upButton));
  }
  if (!digitalRead(selectButton))
  {
    executeAction();
    updateMenu();
    delay(100);
    while (!digitalRead(selectButton));
  }
}
void action3() 
{
  lcd.clear();
  lcd.print(">motor sure");
  lcd.setCursor(14, 0);
  lcd.print(bkl);
  delay(15000);
  
  //h?z artt?r azalt
  if (!digitalRead(downButton))
  {
    bkl +=10000;
    delay(100);
    while (!digitalRead(downButton));
  }
  if (!digitalRead(upButton))
  {
    bkl -=10000;
    delay(100);
    while(!digitalRead(upButton));
  }
  if (!digitalRead(selectButton))
  {
    executeAction();
    updateMenu();
    delay(100);
    while (!digitalRead(selectButton));
  }
}
void action4() 
{
  lcd.clear();
  lcd.print(">sicakli");
  lcd.setCursor(11,0);
  lcd.print(temperature);
  delay(15000);
  
}
